# Fritzing sketch power-supply-with-charger (saved by Fritzing 0.9.3b)
circuit board: 10cm x 5cm
breadboards: 2

parts:
  M1 = RioRand LM2596 [part_number="Power Supply 5 V"]
  J1 = Screw terminal - 2 pins [part_number="Input 12 V" package=THT]
  J2 = Screw terminal - 2 pins [part_number="Output 5 V" package=THT]
  VREG1 = Voltage Regulator - 5V [part_number="Voltage Regulator L4940V5" package="TO220 [THT]"]
  C1 = Capacitor [part_number="100 nF" package=cap-pth-small2]
  J4 = Screw terminal - 2 pins [part_number="Output 5 V" package=THT]
  D1 = Schottky Diode [part_number=20SQ045 package="300 mil [THT]"]
  J5 = Screw terminal - 2 pins [part_number="Input 12 V" package=THT]
  F3 = Resettable Fuse PTC [part_number="Fuse 3A" package=ptc]
  J7 = Screw terminal - 2 pins [part_number="Battery 7.2 V" package=THT]
  M2 = RioRand LM2596 [part_number="Charger 8.4 V"]
  C2 = Capacitor Polarized [part_number="470 uF" package=cpol-radial-100uf-25v]

nets:
  N1: M1.Pin_1, J1.pin1, VREG1.input_voltage, C1.2, D1.cathode, J5.pin1, M2.Pin_1
  GND: M1.Pin_2, M1.Pin_4, J1.pin2, J2.pin2, VREG1.GND, C1.1, J4.pin2, J5.pin2, M2.Pin_2, C2.-
  N2: M1.Pin_3, J2.pin1, VREG1.output_voltage, J4.pin1, C2.+
  N3: D1.anode, F3.1, M2.Pin_3
  N4: F3.2, J7.pin1
  N5: J7.pin2, M2.Pin_4
